# Fritzing sketch Line follower wiring schematic (saved by Fritzing 0.9.6b)
breadboards: 1

parts:
  U1 = L9110 H-bridge module [part_number="L9110 H-bridge"]
  M1 = gear-motor
  M2 = gear-motor
  Part1 = Arduino Uno (Rev3)

nets:
  N1: U1.B-IA, Part1.D5_PWM
  N2: U1.B-IB, Part1.D4
  GND: U1.GND, Part1.GND
  VCC: U1.VCC, Part1.5V
  N3: U1.A-IA, Part1.D3_PWM
  N4: U1.A-IB, Part1.D2
  N5: U1.MOTOR_A-A, M2.pin_1
  N6: U1.MOTOR_A-B, M2.pin_2
  N7: U1.MOTOR_B-A, M1.pin_1
  N8: U1.MOTOR_B-B, M1.pin_2
